# Fritzing sketch breadboard_setup (saved by Fritzing 0.9.3b)
breadboards: 2

parts:
  C2 = Electrolytic Capacitor [capacitance=470µF voltage=16V package="100 mil [THT, electrolytic]"]
  IC1 = Voltage Regulator [package=to220-igo]
  C3 = Electrolytic Capacitor [capacitance=10µF voltage=50V package="100 mil [THT, electrolytic]"]
  J3 = Power Jack [package=power_jack_slot]
  R1 = Resistor [tolerance=±5% resistance=220 package="0805 [SMD]"]
  LED1 = LED - 5mm [color="Red (633nm)" package="5 mm [THT]"]
  U1 = atmega328 [package=dip]
  R2 = Resistor [tolerance=±5% resistance=10k package="0805 [SMD]"]
  C6 = Capacitor [package=cap-pth-small2]
  XTAL2 = CRYSTAL - kHz [frequency="16 Mhz"]
  C7 = Capacitor [package=cap-pth-small2]
  ZS-042_RTC1 = ZS-042 RTC Module
  LCD1 = LCD screen
  R3 = Resistor [tolerance=±5% resistance=1.2k package="0805 [SMD]"]
  Q1 = TRANSISTOR_NPN [package=to-92-ammo]
  R4 = Resistor [tolerance=±5% resistance=10k package="0805 [SMD]"]
  S1 = Pushbutton [package=THT]
  R5 = Resistor [tolerance=±5% resistance=10k package="0805 [SMD]"]

nets:
  GND: C2.-, IC1.IN, C3.-, J3.GNDBREAK, LED1.cathode, U1.GND, C6.2, C7.2, ZS-042_RTC1.GND, LCD1.VSS, LCD1.LED-, R3.Pin_0, R5.Pin_0
  VCC: C2.+, IC1.OUT, R1.Pin_0, U1.VCC, U1.AVCC, U1.AREF, R2.Pin_0, ZS-042_RTC1.VCC, LCD1.VDD, Q1.E, S1.leg0
  N1: IC1.GND, C3.+, J3.PWR
  N2: R1.Pin_1, LED1.anode
  N3: U1.RESET, R2.Pin_1
  N4: U1.D3_(PWM), LCD1.R/W
  N5: U1.D4, LCD1.DB5
  N6: U1.XLAT1, XTAL2.pin_1, C7.1
  N7: U1.XLAT2, C6.1, XTAL2.pin_0
  N8: U1.D5_(PWM), LCD1.DB4
  N9: U1.D6_(PWM), LCD1.DB6
  N10: U1.D7, S1.leg1, R5.Pin_1
  N11: U1.D8, LCD1.DB7
  N12: U1.D11_(PWM), R4.Pin_0
  N13: U1.D12, LCD1.RS
  N14: U1.A4, ZS-042_RTC1.SDA
  N15: U1.A5, ZS-042_RTC1.SCL
  N16: LCD1.V0, R3.Pin_1
  N17: LCD1.LED+, Q1.C
  N18: Q1.B, R4.Pin_1
